// Logisim project processor_riscv_evolution.circ as structural Verilog
module ALU (
  input  [2:0] F,
  input  [31:0] B,
  input  [31:0] A,
  output Zero_flag,
  output Carry_Out,
  output [31:0] Y
);

  wire bit_extender_2_out, comparator_1_eq, comparator_1_gt, comparator_1_lt;
  wire [31:0] adder_1_out, and_1_out, bit_extender_1_out, multiplexer_1_out, not_1_out, or_1_out;

  assign not_1_out = ~B;  // NOT_Gate not_1, 32 bits wide
  Multiplexer #(.width(32)) multiplexer_1 (.in0(B), .in1(not_1_out), .out(multiplexer_1_out), .sel(F[0]));
  Adder #(.width(32)) adder_1 (.a(multiplexer_1_out), .b(A), .out(adder_1_out), .cin(F[0]), .cout(Carry_Out));
  assign and_1_out = A & B;  // AND_Gate and_1, 32 bits wide
  assign or_1_out = A | B;  // OR_Gate or_1, 32 bits wide
  Comparator #(.mode("unsigned"), .width(32)) comparator_1 (
    .a(B), .b(A), .gt(comparator_1_gt), .eq(comparator_1_eq), .lt(comparator_1_lt));
  assign bit_extender_1_out = {{31{1'b0}}, comparator_1_gt};  // Bit_Extender bit_extender_1
  Multiplexer #(.select(3), .width(32)) multiplexer_2 (
    .in0(adder_1_out), .in2(and_1_out), .in3(or_1_out), .in5(bit_extender_1_out), .out(Y));  // open: in1, in4, in6, in7, sel
  Bit_Extender #(.in_width(32), .out_width(1)) bit_extender_2 (.in(Y), .out(bit_extender_2_out));
  nor nor_1 (Zero_flag, bit_extender_2_out, bit_extender_2_out);

  // Notes on the sheet:
  //   B: initial=0xa
  //   A: initial=0x5
  //   F: initial=0x5
endmodule

module Datapath (
  output [31:0] t2
);

  wire clock_1_out;
  wire [7:0] register_1_q, undriven;
  wire [31:0] rom_1_data;

  Clock clock_1 (.out(clock_1_out));
  Register register_1 (.D(undriven), .en(1'b1), .clk(clock_1_out), .Q(register_1_q));  // open: clr
  Shifter #(.shift("lr")) shifter_1 (.in(register_1_q), .\dist (3'b010));  // open: out
  ROM #(.dataWidth(32)) rom_1 (.data(rom_1_data));  // open: addr
  ControlUnit controlunit_1 ();  // open: Instruction, RegWrite, ALUSrc, ALUControl, Branch
endmodule

module RegisterFile (
  input  CLK,
  input  [2:0] A1,
  input  [31:0] WD3,
  input  [2:0] A2,
  input  WE3,
  input  [2:0] A3,
  output [31:0] RD1,
  output [31:0] RD2,
  output [31:0] T2
);

  wire and_1_out, and_2_out, and_3_out, and_4_out, and_5_out, and_6_out, and_7_out, decoder_1_out0,
       decoder_1_out1, decoder_1_out2, decoder_1_out3, decoder_1_out4, decoder_1_out5, decoder_1_out6,
       decoder_1_out7;
  wire [31:0] register_1_q, register_2_q, register_3_q, register_4_q, register_5_q, register_6_q,
       register_7_q, undriven;

  Decoder #(.select(3)) decoder_1 (
    .out0(decoder_1_out0), .out1(decoder_1_out1), .out2(decoder_1_out2), .out3(decoder_1_out3),
    .out4(decoder_1_out4), .out5(decoder_1_out5), .out6(decoder_1_out6), .out7(decoder_1_out7), .sel(A3));  // open: en
  and and_1 (and_1_out, WE3, decoder_1_out1);
  and and_2 (and_2_out, WE3, decoder_1_out2);
  and and_3 (and_3_out, WE3, decoder_1_out3);
  and and_4 (and_4_out, WE3, decoder_1_out4);
  and and_5 (and_5_out, WE3, decoder_1_out5);
  and and_6 (and_6_out, WE3, decoder_1_out6);
  and and_7 (and_7_out, WE3, decoder_1_out7);
  Register #(.width(32)) register_1 (.D(WD3), .en(and_1_out), .clk(CLK), .Q(register_1_q));  // open: clr
  Register #(.width(32)) register_2 (.D(WD3), .en(and_2_out), .clk(CLK), .Q(register_2_q));  // open: clr
  Register #(.width(32)) register_3 (.D(WD3), .en(and_3_out), .clk(CLK), .Q(register_3_q));  // open: clr
  Register #(.width(32)) register_4 (.D(WD3), .en(and_4_out), .clk(CLK), .Q(register_4_q));  // open: clr
  Register #(.width(32)) register_5 (.D(WD3), .en(and_5_out), .clk(CLK), .Q(register_5_q));  // open: clr
  Register #(.width(32)) register_6 (.D(WD3), .en(and_6_out), .clk(CLK), .Q(register_6_q));  // open: clr
  Register #(.width(32)) register_7 (.D(WD3), .en(and_7_out), .clk(CLK), .Q(register_7_q));  // open: clr
  Multiplexer #(.enable("true"), .select(3), .width(32)) multiplexer_1 (
    .in0(undriven), .in1(register_1_q), .in2(register_2_q), .in3(register_3_q), .in4(register_4_q),
    .in5(register_5_q), .in6(register_6_q), .in7(register_7_q), .out(RD1), .sel(A1));  // open: en
  Multiplexer #(.enable("true"), .select(3), .width(32)) multiplexer_2 (
    .in0(undriven), .in1(register_1_q), .in2(register_2_q), .in3(register_3_q), .in4(register_4_q),
    .in5(register_5_q), .in6(register_6_q), .in7(register_7_q), .out(RD2), .sel(A2));  // open: en
endmodule

module ControlUnit (
  input  [31:0] Instruction,
  output RegWrite,
  output ALUSrc,
  output [2:0] ALUControl,
  output Branch
);

  wire comparator_1_eq, comparator_3_eq;

  Comparator #(.mode("unsigned"), .width(7)) comparator_1 (
    .a(Instruction[6:0]), .b(7'b1100011), .eq(comparator_1_eq));  // open: gt, lt
  Comparator #(.mode("unsigned"), .width(7)) comparator_2 (
    .a(Instruction[6:0]), .b(7'b0010011), .eq(ALUSrc));  // open: gt, lt
  Comparator #(.mode("unsigned"), .width(7)) comparator_3 (
    .a(Instruction[6:0]), .b(7'b0110011), .eq(comparator_3_eq));  // open: gt, lt
  or or_1 (RegWrite, ALUSrc, comparator_3_eq);
endmodule

module Tests (
  output [31:0] Y,
  output [3:0] out_2,
  output [7:0] out_3
);


  assign out_2 = 4'b0010;
  assign out_3 = 8'h22;
  assign Y = 32'hf4010207;

  // Notes on the sheet:
  //   binary values in Logisim. Convince yourself how the bits are displayed.
  //   Example 1: A simple example that illustrates how 32-bit values are displayed as 
  //   Example 2) An example of how to extra certain bits from a (in this case) 32-bit wire. Here we extract the bits 8..11 from the 32-bit wire.
  //   Example 3) Sometimes it is useful to extra bits from different position and the re-assemble them. In this case, we extract bits 8..11 and bits 15..18 and assemble them into an 8-bit wire.
endmodule
